# Fritzing sketch 9v button (saved by Fritzing 0.9.3b)
breadboards: 4

parts:
  VCC1 = Battery block 9V
  LED1 = LED - 5mm [color="Red (633nm)" package="5 mm [THT]"]
  R1 = Resistor [tolerance=±5% resistance=330 package=THT]
  S2 = Pushbutton [package="[SMD]"]
  VCC2 = Battery block 9V
  LED2 = LED - 5mm [color="Red (633nm)" package="5 mm [THT]"]
  R2 = Resistor [tolerance=±5% resistance=330 package=THT]
  VCC3 = Battery block 9V
  LED3 = LED - 5mm [color="Red (633nm)" package="5 mm [THT]"]
  R3 = Resistor [tolerance=±5% resistance=330 package=THT]
  LED4 = LED - 5mm [color="Red (633nm)" package="5 mm [THT]"]
  R4 = Resistor [tolerance=±5% resistance=330 package=THT]
  R5 = Resistor [tolerance=±5% resistance=330 package=THT]
  LED5 = LED - 5mm [color="Red (633nm)" package="5 mm [THT]"]
  VCC4 = Battery block 9V
  LED6 = LED - 5mm [color="Red (633nm)" package="5 mm [THT]"]
  LED7 = LED - 5mm [color="Red (633nm)" package="5 mm [THT]"]
  LED8 = LED - 5mm [color="Red (633nm)" package="5 mm [THT]"]
  R7 = Resistor [tolerance=±5% resistance=100 package=THT]

nets:
  N1: VCC1.-, R1.Pin_0
  N2: VCC1.+, LED1.anode
  N3: LED1.cathode, R1.Pin_1
  N4: S2.Pin_1, S2.Pin_2, R2.Pin_0
  N5: S2.Pin_3, S2.Pin_4, LED2.anode
  N6: VCC2.-, LED2.cathode
  N7: VCC2.+, R2.Pin_1
  N8: VCC3.-, R3.Pin_0, R4.Pin_0, R5.Pin_0
  N9: VCC3.+, LED3.anode, LED4.anode, LED5.anode
  N10: LED3.cathode, R3.Pin_1
  N11: LED4.cathode, R4.Pin_1
  N12: R5.Pin_1, LED5.cathode
  N13: VCC4.-, R7.Pin_0
  N14: VCC4.+, LED6.anode
  N15: LED6.cathode, LED8.anode
  N16: LED7.cathode, R7.Pin_1
  N17: LED7.anode, LED8.cathode
