# Fritzing sketch 9v led (saved by Fritzing 1.0.6)
breadboards: 3

parts:
  VCC1 = Battery block 9V [internal_resistance=0.1Ω]
  LED1 = LED - 5mm [color="Red (633nm)" current=0.030A package="5 mm [THT]"]
  R1 = Resistor [tolerance=±5% resistance=330 power=0.25W package=THT]
  VCC3 = Battery block 9V [internal_resistance=0.1Ω]
  LED3 = LED - 5mm [color="Red (633nm)" current=0.030A package="5 mm [THT]"]
  R3 = Resistor [tolerance=±5% resistance=330 power=0.25W package=THT]
  LED4 = LED - 5mm [color="Red (633nm)" current=0.030A package="5 mm [THT]"]
  R4 = Resistor [tolerance=±5% resistance=330 power=0.25W package=THT]
  R5 = Resistor [tolerance=±5% resistance=330 power=0.25W package=THT]
  LED5 = LED - 5mm [color="Red (633nm)" current=0.030A package="5 mm [THT]"]
  VCC4 = Battery block 9V [internal_resistance=0.1Ω]
  LED6 = LED - 5mm [color="Red (633nm)" current=0.030A package="5 mm [THT]"]
  LED7 = LED - 5mm [color="Red (633nm)" current=0.030A package="5 mm [THT]"]
  LED8 = LED - 5mm [color="Red (633nm)" current=0.030A package="5 mm [THT]"]
  R7 = Resistor [tolerance=±5% resistance=100 power=0.25W package=THT]

nets:
  N1: VCC1.-, R1.Pin_0
  N2: VCC1.+, LED1.anode
  N3: LED1.cathode, R1.Pin_1
  N4: VCC3.-, R3.Pin_0, R4.Pin_0, R5.Pin_0
  N5: VCC3.+, LED3.anode, LED4.anode, LED5.anode
  N6: LED3.cathode, R3.Pin_1
  N7: LED4.cathode, R4.Pin_1
  N8: R5.Pin_1, LED5.cathode
  N9: VCC4.-, R7.Pin_0
  N10: VCC4.+, LED6.anode
  N11: LED6.cathode, LED8.anode
  N12: LED7.cathode, R7.Pin_1
  N13: LED7.anode, LED8.cathode
