# Fritzing sketch aa led (saved by Fritzing 1.0.6)

parts:
  LED1 = LED - 5mm [color="Red (633nm)" current=0.030A package="5 mm [THT]"]
  BAT1 = Battery Holders [package=battery-aa]

nets:
  N1: LED1.cathode, BAT1.-
  N2: LED1.anode, BAT1.+
