# Fritzing sketch PWM_LED (saved by Fritzing 0.9.1b)
breadboards: 1

parts:
  Part1 = Arduino Uno (Rev3)
  R7 = Resistor [tolerance=±5% resistance=330 package=THT]
  LED2 = LED - 5mm [color="Red (633nm)" package="5 mm [THT]"]

nets:
  N1: Part1.D9_PWM, R7.Pin_1
  N2: Part1.GND, LED2.cathode
  N3: R7.Pin_0, LED2.anode
