# Fritzing sketch arduino-blink-2 (saved by Fritzing 0.9.1b)

parts:
  Part2 = Arduino Uno (Rev3)
  LED3 = LED - 5mm [color="Red (633nm)" package="5 mm [THT]"]

nets:
  N1: Part2.D13/SCK, LED3.anode
  N2: Part2.GND, LED3.cathode
