# Fritzing sketch arduino-blink-3 (saved by Fritzing 0.9.1b)
breadboards: 1

parts:
  Part2 = Arduino Uno (Rev3)
  LED3 = LED - 5mm [color="Red (633nm)" package="5 mm [THT]"]
  R9 = Resistor [tolerance=±5% resistance=330 package=THT]

nets:
  N1: Part2.D12/MISO, R9.Pin_1
  N2: Part2.GND, LED3.cathode
  N3: LED3.anode, R9.Pin_0
