# Fritzing sketch feather-blink-2 (saved by Fritzing 0.9.4)
breadboards: 1

parts:
  LED3 = LED - 5mm [color="Red (633nm)" package="5 mm [THT]"]
  Part3 = Adafruit Feather 32u4 Basic Proto [part_number="Adafruit #2771"]

nets:
  N1: LED3.cathode, Part3.GND
  N2: LED3.anode, Part3.13

custom parts:
  Adafruit Feather 32u4 Basic Proto: At the Feather 32u4's heart is at ATmega32u4 clocked at 8 MHz and at 3.3V logic, a chip setup we've had tons of experience with as it's the same as the Flora. This chip has 32K of flash and 2K of RAM, with built in USB so not only does it have a USB-to-Serial program & debug capability built in with no need for an FTDI-like chip, it can also act like a mouse, keyboard, USB MIDI device, etc.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
