# Fritzing sketch metro-pwm-led (saved by Fritzing 0.9.3b)
breadboards: 1

parts:
  LED1 = LED - 5mm [color="Red (633nm)" package="5 mm [THT]"]
  R1 = Resistor [tolerance=±5% resistance=150 package="0402 [SMD]"]
  Part1 = Adafruit Feather 32u4 Basic Proto [part_number="Adafruit #2771"]

nets:
  N1: LED1.cathode, Part1.GND
  N2: LED1.anode, R1.Pin_1
  N3: R1.Pin_0, Part1.11

custom parts:
  Adafruit Feather 32u4 Basic Proto: At the Feather 32u4's heart is at ATmega32u4 clocked at 8 MHz and at 3.3V logic, a chip setup we've had tons of experience with as it's the same as the Flora. This chip has 32K of flash and 2K of RAM, with built in USB so not only does it have a USB-to-Serial program & debug capability built in with no need for an FTDI-like chip, it can also act like a mouse, keyboard, USB MIDI device, etc.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
