# Fritzing sketch potentiometer-blink (saved by Fritzing 0.9.1b)
breadboards: 1

parts:
  Part1 = Arduino Uno (Rev3)
  R2 = Rotary Potentiometer (Small) [maximum_resistance=100kΩ package=THT]
  LED2 = LED - 5mm [color="Red (633nm)" package="5 mm [THT]"]

nets:
  N1: Part1.A0, R2.wiper
  N2: Part1.D13/SCK, LED2.anode
  N3: Part1.GND, R2.leg1, LED2.cathode
  N4: Part1.5V, R2.leg2
