# Fritzing sketch potentiometer (saved by Fritzing 0.9.1b)
breadboards: 1

parts:
  Part1 = Arduino Uno (Rev3)
  R2 = Rotary Potentiometer (Small) [maximum_resistance=100kΩ package=THT]
  R7 = Resistor [tolerance=±5% resistance=330 package=THT]
  LED2 = LED - 5mm [color="Red (633nm)" package="5 mm [THT]"]

nets:
  N1: Part1.A0, R2.wiper
  N2: Part1.D9_PWM, R7.Pin_1
  N3: Part1.5V, R2.leg2
  N4: Part1.GND, R2.leg1, LED2.cathode
  N5: R7.Pin_0, LED2.anode
