# Fritzing sketch pwm-led (saved by Fritzing 1.0.6)
breadboards: 1

parts:
  LED3 = LED - 5mm [color="Red (633nm)" current=0.030A package="5 mm [THT]"]
  R9 = Resistor [tolerance=±5% resistance=100 power=0.25W package=THT]
  Part3 = Adafruit Feather 32u4 Basic Proto [part_number="Adafruit #2771"]

nets:
  N1: LED3.cathode, Part3.GND
  N2: LED3.anode, R9.Pin_1
  N3: R9.Pin_0, Part3.9

custom parts:
  Adafruit Feather 32u4 Basic Proto: At the Feather 32u4's heart is at ATmega32u4 clocked at 8 MHz and at 3.3V logic, a chip setup we've had tons of experience with as it's the same as the Flora. This chip has 32K of flash and 2K of RAM, with built in USB so not only does it have a USB-to-Serial program & debug capability built in with no need for an FTDI-like chip, it can also act like a mouse, keyboard, USB MIDI device, etc.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
