# Fritzing sketch audio (saved by Fritzing 1.0.6)
breadboards: 1

parts:
  Part3 = Adafruit Feather 32u4 Basic Proto [part_number="Adafruit #2771"]
  J1 = Piezo Speaker

nets:
  N1: Part3.GND, J1.pin1
  N2: Part3.9, J1.pin2

custom parts:
  Adafruit Feather 32u4 Basic Proto: At the Feather 32u4's heart is at ATmega32u4 clocked at 8 MHz and at 3.3V logic, a chip setup we've had tons of experience with as it's the same as the Flora. This chip has 32K of flash and 2K of RAM, with built in USB so not only does it have a USB-to-Serial program & debug capability built in with no need for an FTDI-like chip, it can also act like a mouse, keyboard, USB MIDI device, etc.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
