# Fritzing sketch LDR (saved by Fritzing 1.0.6)
breadboards: 1

parts:
  Part1 = Adafruit Feather 32u4 Basic Proto [part_number="Adafruit #2771"]
  LED1 = LED - 5mm [color="Red (633nm)" current=0.030A package="5 mm [THT]"]
  R2 = Resistor [tolerance=±5% power=0.25W resistance=100 package=THT]
  R3 = Photocell (LDR) [power=0.25W dark_resistance_@0.01lx=300kΩ light_resistance_@100lx=400Ω luminance=10lx package=THT]
  R4 = Resistor [tolerance=±5% power=0.25W resistance=10k package=THT]

nets:
  N1: Part1.GND, R2.Pin_0, R3.pin_1
  N2: Part1.A0, R3.pin_0, R4.Pin_1
  N3: Part1.+3V3, R4.Pin_0
  N4: Part1.9, LED1.cathode
  N5: LED1.anode, R2.Pin_1

custom parts:
  Adafruit Feather 32u4 Basic Proto: At the Feather 32u4's heart is at ATmega32u4 clocked at 8 MHz and at 3.3V logic, a chip setup we've had tons of experience with as it's the same as the Flora. This chip has 32K of flash and 2K of RAM, with built in USB so not only does it have a USB-to-Serial program & debug capability built in with no need for an FTDI-like chip, it can also act like a mouse, keyboard, USB MIDI device, etc.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
