# Fritzing sketch potentiometer (saved by Fritzing 1.0.6)
breadboards: 1

parts:
  Part1 = Adafruit Feather 32u4 Basic Proto [part_number="Adafruit #2771"]
  R1 = Rotary Potentiometer (Small) [maximum_resistance=100kΩ knob_status=50% power=0.5W package=THT]

nets:
  N1: Part1.GND, R1.leg2
  N2: Part1.A0, R1.wiper
  N3: Part1.+3V3, R1.leg1

custom parts:
  Adafruit Feather 32u4 Basic Proto: At the Feather 32u4's heart is at ATmega32u4 clocked at 8 MHz and at 3.3V logic, a chip setup we've had tons of experience with as it's the same as the Flora. This chip has 32K of flash and 2K of RAM, with built in USB so not only does it have a USB-to-Serial program & debug capability built in with no need for an FTDI-like chip, it can also act like a mouse, keyboard, USB MIDI device, etc.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
