# Fritzing sketch DRV8871 (saved by Fritzing 0.9.4)
breadboards: 1

parts:
  Part1 = Adafruit DRV8871 [part_number="Adafruit #3190"]
  Part2 = Adafruit Feather 32u4 Basic Proto [part_number="Adafruit #2771"]
  M1 = DC Motor
  VCC1 = Battery block 9V

nets:
  N1: Part1.GND, VCC1.-
  N2: Part1.VMOTOR, VCC1.+
  N3: Part1.IN1, Part2.10
  N4: Part1.IN2, Part2.9
  N5: Part1.OUT2, M1.pin_1
  N6: Part1.OUT1, M1.pin_2

custom parts:
  Adafruit DRV8871: Crank up your robotics with powerful Adafruit DRV8871 motor driver breakout board. This motor driver has a lot of great specs that make it useful for a wide variety of mechatronics. In particular, the simple resistor-set current limiting and auto-magic PWM support make it super easy to use. Check out the specs for the DRV8871: 6.5V to 45V motor power voltage Up to 5.5V logic level on IN pins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
  Adafruit Feather 32u4 Basic Proto: At the Feather 32u4's heart is at ATmega32u4 clocked at 8 MHz and at 3.3V logic, a chip setup we've had tons of experience with as it's the same as the Flora. This chip has 32K of flash and 2K of RAM, with built in USB so not only does it have a USB-to-Serial program & debug capability built in with no need for an FTDI-like chip, it can also act like a mouse, keyboard, USB MIDI device, etc.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
