# Fritzing sketch h-bridge-motor (saved by Fritzing 0.8.5b)
breadboards: 1

parts:
  Part2 = Arduino Uno (Rev3)
  IC1 = H-Bridge [package=THT]
  M2 = DC Motor
  VCC1 = Battery block 9V

nets:
  N1: Part2.D9_PWM, IC1.1_2EN
  GND: Part2.GND, IC1.GND1, IC1.GND2, IC1.GND3, IC1.GND4, VCC1.-
  N2: Part2.D3_PWM, IC1.2A
  N3: Part2.D4, IC1.1A
  N4: Part2.5V, IC1.VCC1
  N5: IC1.1Y, M2.pin_1
  N6: IC1.2Y, M2.pin_2
  N7: IC1.VCC2, VCC1.+
