# Fritzing sketch mosfet-led (saved by Fritzing 0.9.4)
breadboards: 1

parts:
  TIP-120 = Basic FET P-Channel [part_number=TIP-120 package="TO220 [THT]"]
  Part2 = Adafruit Feather 32u4 Basic Proto [part_number="Adafruit #2771"]
  R1 = Resistor [tolerance=±5% resistance=10k package="0603 [SMD]"]
  LED1 = LED - 5mm [color="Red (633nm)" package="5 mm [THT]"]
  R2 = Resistor [tolerance=±5% resistance=220 package="0603 [SMD]"]

nets:
  N1: TIP-120.gate, Part2.5, R1.Pin_1
  N2: TIP-120.drain, LED1.cathode
  N3: TIP-120.source, Part2.GND, R1.Pin_0
  N4: Part2.VBUS, R2.Pin_1
  N5: LED1.anode, R2.Pin_0

custom parts:
  Adafruit Feather 32u4 Basic Proto: At the Feather 32u4's heart is at ATmega32u4 clocked at 8 MHz and at 3.3V logic, a chip setup we've had tons of experience with as it's the same as the Flora. This chip has 32K of flash and 2K of RAM, with built in USB so not only does it have a USB-to-Serial program & debug capability built in with no need for an FTDI-like chip, it can also act like a mouse, keyboard, USB MIDI device, etc.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
