# Fritzing sketch mosfet-motor (saved by Fritzing 0.9.4)
breadboards: 1

parts:
  TIP-120 = Basic FET P-Channel [part_number=TIP-120 package="TO220 [THT]"]
  M1 = DC Motor
  Part2 = Adafruit Feather 32u4 Basic Proto [part_number="Adafruit #2771"]
  D1 = Diode [package=diode-1n4001]
  R1 = Resistor [tolerance=±5% resistance=10k package="0603 [SMD]"]
  VCC1 = Battery block 9V

nets:
  N1: TIP-120.gate, Part2.5, R1.Pin_1
  N2: TIP-120.drain, M1.pin_2
  N3: TIP-120.source, Part2.GND, R1.Pin_0, VCC1.-
  N4: M1.pin_1, D1.C, VCC1.+

custom parts:
  Adafruit Feather 32u4 Basic Proto: At the Feather 32u4's heart is at ATmega32u4 clocked at 8 MHz and at 3.3V logic, a chip setup we've had tons of experience with as it's the same as the Flora. This chip has 32K of flash and 2K of RAM, with built in USB so not only does it have a USB-to-Serial program & debug capability built in with no need for an FTDI-like chip, it can also act like a mouse, keyboard, USB MIDI device, etc.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
